# Fritzing sketch meteos-sensor-circuit (saved by Fritzing 0.9.3b)

parts:
  M1 = DOIT Esp32 DevKit v1 (30 pins long, 11 pins width) [part_number=ESP32S-PIN30]
  Part1 = BME280 Breakout
  ncr18650b = 18650 battery holder [package=battery-18650-kit]
  TP1 = TP4056 [chip_label=TP4056 package="DIP (Dual Inline) [THT]"]
  OLED1 = OLED 128x64 I2C Monochrome Display
  S2 = Momentary Switch [package=ksa_sealed_tac_switch]
  IC1 = IC, DIP package, 4 pins [chip_label=DC-DC]
  S3 = Toggle Switch [package=THT]
  TD-er1 = MH-Z19 CO2 sensor [part_number=MH-Z19]
  C1 = Electrolytic Capacitor [capacitance=1mF package="100 mil [THT, electrolytic]"]

nets:
  3V3: M1.3V3, Part1.3.3V, OLED1.VDD
  GND: M1.GND, Part1.GND, OLED1.GND, S2.3, IC1.pin2, TD-er1.GND, C1.-
  N1: M1.D15, S2.1
  N2: M1.D21, Part1.SDI/SDA, OLED1.SDA
  N3: M1.D22, Part1.SCK/SCL, OLED1.SCK
  N4: M1.VIN, IC1.pin1, C1.+
  N5: ncr18650b.+, TP1.pin4
  N6: ncr18650b.-, TP1.pin5
  N7: TP1.pin3, S3.COM
  N8: TP1.pin6, IC1.pin4
  N9: IC1.pin3, S3.L2

custom parts:
  DOIT Esp32 DevKit v1 (30 pins long, 11 pins width): The DOIT Esp32 DevKit v1 is one of the development board created by DOIT to evaluate the ESP-WROOM-32 module. It is based on the ESP32 microcontroller that boasts Wifi, Bluetooth, Ethernet and Low Power support all in a single chip. (vanepp) made breadboard work, adjusted pin numbering and labels and reduced size of schematic and cleaned up pcb. This chip is 30pins long (2 x15) and 11 pins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
  18650 battery holder: 18650 Battery Holder
  TP4056: A DIP stand-in part for whatever IC you want. With 6 pins on a 300mil dual inline package (DIP) footprint.
